// Digital circuit 4_bit_processing_Complete(CPU4bit).dig as structural Verilog
module _4_bit_processing_Complete_CPU4bit (
  input  [3:0] InstructionMemory_dataInput,
  input  [1:0] InstructionMemory_ctrl,
  input  clk,
  input  [3:0] Dummy,
  output PC_inc,
  output [4:0] state,
  output IR_LO_Write,
  output IR_HI_Write,
  output [3:0] IP,
  output [1:0] IR_HI_3_2,
  output [1:0] IR_LO_1_0,
  output [1:0] IR_LO_3_2,
  output [3:0] Mem,
  output [3:0] ALU_out,
  output [1:0] IR_HI_1_0
);

  wire and_4_out, control_rtype_1_writeback, not_2_out, xor_1_out;
  wire [1:0] multiplexer_1_out, multiplexer_2_out, multiplexer_3_out, multiplexer_7_out, not_1_out;
  wire [2:0] and_1_out;
  wire [3:0] demultiplexer_1_out_0, demultiplexer_1_out_1, InstructionMemory_data_output, multiplexer_6_out,
       multiplexer_8_out, register_file_1_readdata_1, register_file_1_readdata_2;
  wire [7:0] multiplexer_4_out, multiplexer_5_out;

  Multiplexer #(.Bits(2)) multiplexer_1 (.sel(PC_inc), .in_0(2'b10), .in_1(2'b11), .out(multiplexer_1_out));
  CIS310_GPR_HW2 cis310_gpr_hw2_1 (
    .Input(4'b0000), .Clk(clk), .Input_2(4'b0001), .Store_Clear_Load_Increment(multiplexer_1_out), .Output(IP));
  CIS310_DRAM_HW2 InstructionMemory (
    .Address_bits(IP), .Clock(clk), .Clear_Store_Load(InstructionMemory_ctrl),
    .Data_Input(InstructionMemory_dataInput), .Data_Output(InstructionMemory_data_output));
  Demultiplexer #(.Bits(4)) demultiplexer_1 (
    .sel(IP[0]), .in(InstructionMemory_data_output), .out_0(demultiplexer_1_out_0),
    .out_1(demultiplexer_1_out_1));
  Control_RType control_rtype_1 (
    .clk(clk), .States(state), .IR_HI_Write(IR_HI_Write), .IR_LO_Write(IR_LO_Write),
    .Writeback(control_rtype_1_writeback), .Increment_pc(PC_inc));
  Multiplexer #(.Bits(2)) multiplexer_2 (.sel(IR_HI_Write), .in_0(2'b10), .in_1(2'b01), .out(multiplexer_2_out));
  Multiplexer #(.Bits(2)) multiplexer_3 (.sel(IR_LO_Write), .in_0(2'b10), .in_1(2'b01), .out(multiplexer_3_out));
  CIS310_GPR_1__HW2 Instruction_Register__HI (
    .Input(demultiplexer_1_out_0), .Store_Clear_Load_Increment(multiplexer_2_out), .clk(clk),
    .Output({IR_HI_1_0, IR_HI_1_0}));
  CIS310_GPR_1__HW2 Instruction_Register__LO (
    .Input(demultiplexer_1_out_1), .Store_Clear_Load_Increment(multiplexer_3_out), .clk(clk),
    .Output({IR_HI_1_0, IR_HI_1_0}));
  assign not_1_out = ~IR_HI_1_0;  // Not not_1, 2 bits wide
  Multiplexer #(.Selector_Bits(2), .Bits(8)) multiplexer_4 (
    .sel(IR_HI_1_0), .in_0(8'h1), .in_1(8'h1), .in_2(8'h1), .in_3(8'h1), .out(multiplexer_4_out));
  not not_2 (not_2_out, IR_HI_1_0[1]);
  xor xor_1 (xor_1_out, IR_HI_1_0[1], IR_HI_1_0[0]);
  Multiplexer #(.Bits(8)) multiplexer_5 (
    .sel(control_rtype_1_writeback), .in_0(8'h1), .in_1(multiplexer_4_out), .out(multiplexer_5_out));
  and and_1 (and_1_out[2], IR_HI_1_0[0], IR_HI_1_0[1], not_1_out[0], not_1_out[1]);
  and and_2 (and_1_out[1], not_1_out[1], not_1_out[0], IR_HI_1_0[0], not_2_out);
  Register_file register_file_1 (
    .clock(clk), .ReadRegister_1(IR_HI_1_0), .ReadRegister_2(IR_HI_1_0), .Control_Signals(multiplexer_5_out),
    .Write_Data(multiplexer_8_out), .Write_Register(IR_HI_1_0), .ReadData_1(register_file_1_readdata_1),
    .ReadData_2(register_file_1_readdata_2));
  and and_3 (and_1_out[0], xor_1_out, not_1_out[0], not_1_out[1]);
  Multiplexer #(.Bits(4)) multiplexer_6 (
    .sel(and_4_out), .in_0(register_file_1_readdata_2), .in_1({IR_HI_1_0, IR_HI_1_0}), .out(multiplexer_6_out));
  and and_4 (and_4_out, IR_HI_1_0[0], IR_HI_1_0[1]);
  Multiplexer #(.Bits(2)) multiplexer_7 (.sel(IR_HI_1_0[0]), .in_0(2'b10), .in_1(IR_HI_1_0), .out(multiplexer_7_out));
  _4Bit_ALU _4bit_alu_1 (
    .A(register_file_1_readdata_1), .S_1_S_0_C_in(and_1_out), .B(multiplexer_6_out), .D(ALU_out));  // open: C_out
  CIS310_DRAM_HW2 cis310_dram_hw2_1 (
    .Address_bits({2'b00, IR_HI_1_0}), .Clock(clk), .Clear_Store_Load(multiplexer_7_out),
    .Data_Input(register_file_1_readdata_1), .Data_Output(Mem));
  Multiplexer #(.Selector_Bits(2), .Bits(4)) multiplexer_8 (
    .sel(IR_HI_1_0), .in_0(ALU_out), .in_1(Mem), .in_2({IR_HI_1_0, IR_HI_1_0}), .in_3(Dummy),
    .out(multiplexer_8_out));

  assign IR_HI_3_2 = IR_HI_1_0;
  assign IR_LO_1_0 = IR_HI_1_0;
  assign IR_LO_3_2 = IR_HI_1_0;
endmodule

/* Test case:
# --- Test: program Instruction Memory via buses and run a small program ---
# Program:
#   0/1 : LDI R1,#5   (HI=9,  LO=5)
#   2/3 : LDI R2,#3   (HI=10, LO=3)
#   4/5 : ADD R2,R1   (HI=2,  LO=4)  ; ALU_out should be 8 during execute
#   6/7 : SUB R2,R1   (HI=2,  LO=5)  ; ALU_out should be 3 during execute

clk state PC_inc IP InstructionMemory_dataInput InstructionMemory_ctrl IR-HI-Write IR-LO-Write IR_HI[3:2] IR_HI[1:0] IR_LO[3:2] IR_LO[1:0] ALU_out

# =========================================================
# 1. PROGRAM INSTRUCTION MEMORY USING NORMAL INTERFACE
# ---------------------------------------------------------
# We rely on your control unit / PC_inc to step through IF1/IF2,
# and we just provide the data nibble and InstructionMemory_ctrl
# to store HI/LO nibbles at successive addresses.
#
# Addresses and nibbles:
#   addr 0 : 0x9  (HI of LDI R1,#5)
#   addr 1 : 0x5  (LO of LDI R1,#5)
#   addr 2 : 0xA  (HI of LDI R2,#3)
#   addr 3 : 0x3  (LO of LDI R2,#3)
#   addr 4 : 0x2  (HI of ADD R2,R1)
#   addr 5 : 0x4  (LO of ADD R2,R1)
#   addr 6 : 0x2  (HI of SUB R2,R1)
#   addr 7 : 0x5  (LO of SUB R2,R1)
# =========================================================

# Spin FSM / PC into a stable starting state (as you were doing before)
repeat(39) C X X X 0 0 X X X X X X X
*/
