// Digital circuit CIS310_DRAM_HW2.dig as structural Verilog
module CIS310_DRAM_HW2 (
  input  [3:0] Address_bits,
  input  Clock,
  input  [1:0] Clear_Store_Load,
  input  [3:0] Data_Input,
  output [3:0] Data_Output
);

  wire and_1_out, and_2_out, and_3_out, and_4_out, and_5_out, and_6_out, and_7_out, and_8_out, and_9_out,
       and_10_out, and_11_out, and_12_out, and_13_out, and_14_out, and_15_out, and_16_out, decoder_1_out_0,
       decoder_1_out_1, decoder_1_out_2, decoder_1_out_3, decoder_1_out_4, decoder_1_out_5, decoder_1_out_6,
       decoder_1_out_7, decoder_1_out_8, decoder_1_out_9, decoder_1_out_10, decoder_1_out_11,
       decoder_1_out_12, decoder_1_out_13, decoder_1_out_14, decoder_1_out_15;
  wire [3:0] Row_0_output, Row_1_output, Row_2_output, Row_3_output, Row_4_output, Row_5_output,
       Row_6_output, Row_7_output, Row_8_output, Row_9_output, Row_10_output, Row_11_output, Row_12_output,
       Row_13_output, Row_14_output, Row_15_output;

  Decoder #(.Selector_Bits(4)) decoder_1 (
    .sel(Address_bits), .out_0(decoder_1_out_0), .out_1(decoder_1_out_1), .out_2(decoder_1_out_2),
    .out_3(decoder_1_out_3), .out_4(decoder_1_out_4), .out_5(decoder_1_out_5), .out_6(decoder_1_out_6),
    .out_7(decoder_1_out_7), .out_8(decoder_1_out_8), .out_9(decoder_1_out_9), .out_10(decoder_1_out_10),
    .out_11(decoder_1_out_11), .out_12(decoder_1_out_12), .out_13(decoder_1_out_13),
    .out_14(decoder_1_out_14), .out_15(decoder_1_out_15));
  and and_1 (and_1_out, decoder_1_out_0, Clock);
  and and_2 (and_2_out, decoder_1_out_4, Clock);
  and and_3 (and_3_out, decoder_1_out_8, Clock);
  and and_4 (and_4_out, decoder_1_out_12, Clock);
  CIS_310_GPR2 Row_0 (
    .clk(and_1_out), .Input(Data_Input), .Store_Clear_Load_Increment(Clear_Store_Load), .Output(Row_0_output));
  CIS_310_GPR2 Row_4 (
    .clk(and_2_out), .Input(Data_Input), .Store_Clear_Load_Increment(Clear_Store_Load), .Output(Row_4_output));
  CIS_310_GPR2 Row_8 (
    .clk(and_3_out), .Input(Data_Input), .Store_Clear_Load_Increment(Clear_Store_Load), .Output(Row_8_output));
  CIS_310_GPR2 Row_12 (
    .clk(and_4_out), .Input(Data_Input), .Store_Clear_Load_Increment(Clear_Store_Load), .Output(Row_12_output));
  and and_5 (and_5_out, decoder_1_out_5, Clock);
  and and_6 (and_6_out, decoder_1_out_9, Clock);
  and and_7 (and_7_out, decoder_1_out_13, Clock);
  and and_8 (and_8_out, decoder_1_out_1, Clock);
  CIS_310_GPR2 Row_1 (
    .clk(and_8_out), .Input(Data_Input), .Store_Clear_Load_Increment(Clear_Store_Load), .Output(Row_1_output));
  CIS_310_GPR2 Row_5 (
    .clk(and_5_out), .Input(Data_Input), .Store_Clear_Load_Increment(Clear_Store_Load), .Output(Row_5_output));
  CIS_310_GPR2 Row_9 (
    .clk(and_6_out), .Input(Data_Input), .Store_Clear_Load_Increment(Clear_Store_Load), .Output(Row_9_output));
  CIS_310_GPR2 Row_13 (
    .clk(and_7_out), .Input(Data_Input), .Store_Clear_Load_Increment(Clear_Store_Load), .Output(Row_13_output));
  and and_9 (and_9_out, decoder_1_out_2, Clock);
  and and_10 (and_10_out, decoder_1_out_6, Clock);
  and and_11 (and_11_out, decoder_1_out_10, Clock);
  and and_12 (and_12_out, decoder_1_out_14, Clock);
  CIS_310_GPR2 Row_2 (
    .clk(and_9_out), .Input(Data_Input), .Store_Clear_Load_Increment(Clear_Store_Load), .Output(Row_2_output));
  CIS_310_GPR2 Row_6 (
    .clk(and_10_out), .Input(Data_Input), .Store_Clear_Load_Increment(Clear_Store_Load), .Output(Row_6_output));
  CIS_310_GPR2 Row_10 (
    .clk(and_11_out), .Input(Data_Input), .Store_Clear_Load_Increment(Clear_Store_Load),
    .Output(Row_10_output));
  CIS_310_GPR2 Row_14 (
    .clk(and_12_out), .Input(Data_Input), .Store_Clear_Load_Increment(Clear_Store_Load),
    .Output(Row_14_output));
  and and_13 (and_13_out, decoder_1_out_3, Clock);
  and and_14 (and_14_out, decoder_1_out_7, Clock);
  and and_15 (and_15_out, decoder_1_out_11, Clock);
  and and_16 (and_16_out, decoder_1_out_15, Clock);
  CIS_310_GPR2 Row_3 (
    .clk(and_13_out), .Input(Data_Input), .Store_Clear_Load_Increment(Clear_Store_Load), .Output(Row_3_output));
  CIS_310_GPR2 Row_7 (
    .clk(and_14_out), .Input(Data_Input), .Store_Clear_Load_Increment(Clear_Store_Load), .Output(Row_7_output));
  CIS_310_GPR2 Row_11 (
    .clk(and_15_out), .Input(Data_Input), .Store_Clear_Load_Increment(Clear_Store_Load),
    .Output(Row_11_output));
  CIS_310_GPR2 Row_15 (
    .clk(and_16_out), .Input(Data_Input), .Store_Clear_Load_Increment(Clear_Store_Load),
    .Output(Row_15_output));
  Multiplexer #(.Selector_Bits(4), .Bits(4)) multiplexer_1 (
    .sel(Address_bits), .in_0(Row_0_output), .in_1(Row_1_output), .in_2(Row_2_output), .in_3(Row_3_output),
    .in_4(Row_4_output), .in_5(Row_5_output), .in_6(Row_6_output), .in_7(Row_7_output), .in_8(Row_8_output),
    .in_9(Row_9_output), .in_10(Row_10_output), .in_11(Row_11_output), .in_12(Row_12_output),
    .in_13(Row_13_output), .in_14(Row_14_output), .in_15(Row_15_output), .out(Data_Output));

  // Notes on the sheet:
  //   Clear_Store_Load: 0 -> Clear
  //   1 -> Store input
  //   2 -> Load 
  //   3 -> Set F
endmodule
