// Digital circuit CIS310_GPR(1)_HW2.dig as structural Verilog
module CIS310_GPR_1__HW2 (
  input  [3:0] Input,
  input  [3:0] Store_Clear_Load_Increment,
  input  clk,
  output [3:0] Output
);

  wire [3:0] multiplexer_1_out;

  Multiplexer #(.Selector_Bits(2), .Bits(4)) multiplexer_1 (
    .sel(Store_Clear_Load_Increment[1:0]), .in_0(4'b0000), .in_1(Input), .in_2(Output), .in_3(4'b1111),
    .out(multiplexer_1_out));
  D_FF d_ff_1 (.D(multiplexer_1_out[3]), .C(clk), .Q(Output[3]));  // open: nQ
  D_FF d_ff_2 (.D(multiplexer_1_out[2]), .C(clk), .Q(Output[2]));  // open: nQ
  D_FF d_ff_3 (.D(multiplexer_1_out[1]), .C(clk), .Q(Output[1]));  // open: nQ
  D_FF d_ff_4 (.D(multiplexer_1_out[0]), .C(clk), .Q(Output[0]));  // open: nQ
  // Pins of 2 and 4 bits meet at Store_Clear_Load_Increment

  // Notes on the sheet:
  //   Store_Clear_Load_Increment: 0->Clear
  //   1->Store Input
  //   2->Load
  //   3->Set F
endmodule
