// Digital circuit CIS310_GPR_HW2.dig as structural Verilog
module CIS310_GPR_HW2 (
  input  [3:0] Input,
  input  Clk,
  input  [3:0] Input_2,
  input  [1:0] Store_Clear_Load_Increment,
  output [3:0] Output
);

  wire [3:0] add_1_s, multiplexer_1_out;

  Add #(.Bits(4)) add_1 (.a(Output), .b(Input_2), .c_i(1'b0), .s(add_1_s));  // open: c_o
  Multiplexer #(.Selector_Bits(2), .Bits(4)) multiplexer_1 (
    .sel(Store_Clear_Load_Increment), .in_0(4'b0000), .in_1(Input), .in_2(Output), .in_3(add_1_s),
    .out(multiplexer_1_out));
  D_FF d_ff_1 (.D(multiplexer_1_out[0]), .C(Clk), .Q(Output[0]));  // open: nQ
  D_FF d_ff_2 (.D(multiplexer_1_out[1]), .C(Clk), .Q(Output[1]));  // open: nQ
  D_FF d_ff_3 (.D(multiplexer_1_out[2]), .C(Clk), .Q(Output[2]));  // open: nQ
  D_FF d_ff_4 (.D(multiplexer_1_out[3]), .C(Clk), .Q(Output[3]));  // open: nQ

  // Notes on the sheet:
  //   Input_2: default 1
  //   Store_Clear_Load_Increment: 0->Clear
  //   1->Store input
  //   2->Load
  //   3->Set F
endmodule
