// Digital circuit Control_RType.dig as structural Verilog
module Control_RType (
  input  clk,
  output [4:0] States,
  output IR_HI_Write,
  output IR_LO_Write,
  output Writeback,
  output Increment_pc
);

  D_FF #(.Default(1)) IF1 (.D(States[4]), .C(clk), .Q(IR_HI_Write));  // open: nQ
  D_FF IF2 (.D(IR_HI_Write), .C(clk), .Q(IR_LO_Write));  // open: nQ
  D_FF Decode (.D(IR_LO_Write), .C(clk), .Q(States[2]));  // open: nQ
  D_FF Execute (.D(States[2]), .C(clk), .Q(States[3]));  // open: nQ
  or or_1 (Increment_pc, IR_HI_Write, States[4]);
  D_FF u_WriteBack (.D(States[3]), .C(clk), .Q(States[4]));  // open: nQ

  assign States[1:0] = {IR_LO_Write, IR_HI_Write};
  assign Writeback = States[4];
endmodule
