// Digital circuit Register_file.dig as structural Verilog
module Register_file (
  input  clock,
  input  [1:0] ReadRegister_1,
  input  [1:0] ReadRegister_2,
  input  [7:0] Control_Signals,
  input  [3:0] Write_Data,
  input  [1:0] Write_Register,
  output [3:0] ReadData_1,
  output [3:0] ReadData_2
);

  wire [3:0] demultiplexer_1_out_0, demultiplexer_1_out_1, demultiplexer_1_out_2, demultiplexer_1_out_3,
       R_0_output, R_1_output, R_2_output, R_3_output;

  Demultiplexer #(.Selector_Bits(2), .Bits(4)) demultiplexer_1 (
    .sel(Write_Register), .in(Write_Data), .out_0(demultiplexer_1_out_0), .out_1(demultiplexer_1_out_1),
    .out_2(demultiplexer_1_out_2), .out_3(demultiplexer_1_out_3));
  CIS_310_GPR2 R_0 (
    .clk(clock), .Input(demultiplexer_1_out_0), .Store_Clear_Load_Increment(Control_Signals[1:0]),
    .Output(R_0_output));
  CIS_310_GPR2 R_1 (
    .clk(clock), .Input(demultiplexer_1_out_1), .Store_Clear_Load_Increment(Control_Signals[3:2]),
    .Output(R_1_output));
  CIS_310_GPR2 R_2 (
    .clk(clock), .Input(demultiplexer_1_out_2), .Store_Clear_Load_Increment(Control_Signals[5:4]),
    .Output(R_2_output));
  CIS_310_GPR2 R_3 (
    .clk(clock), .Input(demultiplexer_1_out_3), .Store_Clear_Load_Increment(Control_Signals[7:6]),
    .Output(R_3_output));
  Multiplexer #(.Selector_Bits(2), .Bits(4)) multiplexer_1 (
    .sel(ReadRegister_1), .in_0(R_0_output), .in_1(R_1_output), .in_2(R_2_output), .in_3(R_3_output),
    .out(ReadData_1));
  Multiplexer #(.Selector_Bits(2), .Bits(4)) multiplexer_2 (
    .sel(ReadRegister_2), .in_0(R_0_output), .in_1(R_1_output), .in_2(R_2_output), .in_3(R_3_output),
    .out(ReadData_2));
endmodule
